# Fritzing sketch lightservo (saved by Fritzing 0.9.2b)

parts:
  Part1 = Arduino Mega 2560 (Rev3)
  R1 = PHOTOCELL [package=photocell]
  R2 = Resistor [tolerance=±1% resistance=10k package="2512 [SMD]"]
  R3 = PHOTOCELL [package=photocell]
  R4 = Resistor [tolerance=±1% resistance=10k package="2512 [SMD]"]
  J1 = Basic Servo

nets:
  N1: Part1.5V, R1.P$1
  N2: Part1.D2_PWM, J1.pulse
  N3: R1.P$2, R2.Pin_0
  N4: R3.P$2, R4.Pin_0
  N5: R4.Pin_1, J1.gnd
