# Fritzing sketch testtemperature (saved by Fritzing 0.9.2b)

parts:
  Part1 = Arduino Mega 2560 (Rev3)
  DS1 = DS18B20 1-Wire Temperature Sensor [part_number=DS18B20]
  Part2 = Adafruit ADS1115 16Bit I2C ADC [part_number="Adafruit #1085"]
  Part4 = Adafruit Thermocouple Amplifier MAX31855 [part_number="Adafruit #269"]

nets:
  N1: Part1.D21/SCL, Part2.SCL
  N2: Part1.D20/SDA, Part2.SDA
  5V: Part1.5V, DS1.VDD
  GND: Part1.GND, DS1.GND
  N3: Part1.D2_PWM, DS1.DQ
  N4: Part1.D3_PWM, Part4.DO
  N5: Part1.D4_PWM, Part4.CS
  N6: Part1.D5_PWM, Part4.CLK

custom parts:
  Adafruit ADS1115 16Bit I2C ADC: For microcontrollers without an analog-to-digital converter or when you want a higher-precision ADC, the ADS1115 provides 16-bit precision at 860 samples/second over I2C. The chip can be configured as 4 single-ended input channels, or two differential channels. As a nice bonus, it even includes a programmable gain amplifier, up to x16, to help boost up smaller single/differential signals to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
  Adafruit Thermocouple Amplifier MAX31855: Thermocouples are very sensitive, requiring a good amplifier with a cold-compensation reference. The MAX31855K does everything for you, and can be easily interfaced with any microcontroller, even one without an analog input. This breakout board has the chip itself, a 3.3V regulator with 10uF bypass capacitors and level shifting circuitry, all assembled and tested. Comes with a 2 pin terminal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
